// Logisim project FullAdder.circ as structural Verilog: 14 circuits, main circuit main
module main (
);

  wire adder_8_bit_1_c_out, adder_8_bit_1_o1, adder_8_bit_1_o2, adder_8_bit_1_o3, adder_8_bit_1_o4,
       adder_8_bit_1_o5, adder_8_bit_1_o6, adder_8_bit_1_o7, adder_8_bit_1_o8, and_8_bit_1_o1,
       and_8_bit_1_o2, and_8_bit_1_o3, and_8_bit_1_o4, and_8_bit_1_o5, and_8_bit_1_o6, and_8_bit_1_o7,
       and_8_bit_1_o8, button_1_out, dipswitch_1_sw1, dipswitch_1_sw2, dipswitch_1_sw3, dipswitch_1_sw4,
       dipswitch_1_sw5, dipswitch_1_sw6, dipswitch_1_sw7, dipswitch_1_sw8, dipswitch_2_sw1, dipswitch_2_sw2,
       dipswitch_2_sw3, dipswitch_2_sw4, dipswitch_2_sw5, dipswitch_2_sw6, dipswitch_2_sw7, dipswitch_2_sw8,
       dipswitch_3_sw1, dipswitch_3_sw2, dipswitch_3_sw3, dipswitch_3_sw4, dipswitch_3_sw5, dipswitch_3_sw6,
       dipswitch_3_sw7, dipswitch_3_sw8, dipswitch_4_sw1, dipswitch_4_sw2, dipswitch_4_sw3, dipswitch_4_sw4,
       dipswitch_4_sw5, dipswitch_4_sw6, dipswitch_4_sw7, dipswitch_4_sw8, dipswitch_5_sw1, dipswitch_5_sw2,
       dipswitch_5_sw3, dipswitch_5_sw4, dipswitch_5_sw5, dipswitch_5_sw6, dipswitch_5_sw7, dipswitch_5_sw8,
       dipswitch_6_sw1, dipswitch_6_sw2, dipswitch_6_sw3, dipswitch_6_sw4, dipswitch_6_sw5, dipswitch_6_sw6,
       dipswitch_6_sw7, dipswitch_6_sw8, dipswitch_7_sw1, dipswitch_7_sw2, dipswitch_7_sw3, dipswitch_7_sw4,
       dipswitch_7_sw5, dipswitch_7_sw6, dipswitch_7_sw7, dipswitch_7_sw8, dipswitch_8_sw1, dipswitch_8_sw2,
       dipswitch_9_sw1, dipswitch_9_sw2, dipswitch_9_sw3, dipswitch_9_sw4, dipswitch_9_sw5, dipswitch_9_sw6,
       dipswitch_9_sw7, dipswitch_9_sw8, dipswitch_10_sw1, dipswitch_10_sw2, dipswitch_10_sw3,
       dipswitch_10_sw4, dipswitch_10_sw5, dipswitch_10_sw6, dipswitch_10_sw7, dipswitch_10_sw8,
       mux_8_bit_4_to_1_1_o1, mux_8_bit_4_to_1_1_o2, mux_8_bit_4_to_1_1_o3, mux_8_bit_4_to_1_1_o4,
       mux_8_bit_4_to_1_1_o5, mux_8_bit_4_to_1_1_o6, mux_8_bit_4_to_1_1_o7, mux_8_bit_4_to_1_1_o8,
       or_8_bit_1_o1, or_8_bit_1_o2, or_8_bit_1_o3, or_8_bit_1_o4, or_8_bit_1_o5, or_8_bit_1_o6,
       or_8_bit_1_o7, or_8_bit_1_o8, register8_1_q1, register8_1_q2, register8_1_q3, register8_1_q4,
       register8_1_q5, register8_1_q6, register8_1_q7, register8_1_q8, xor_8_bit_1_o1, xor_8_bit_1_o2,
       xor_8_bit_1_o3, xor_8_bit_1_o4, xor_8_bit_1_o5, xor_8_bit_1_o6, xor_8_bit_1_o7, xor_8_bit_1_o8;

  DipSwitch dipswitch_1 (
    .sw1(dipswitch_1_sw1), .sw2(dipswitch_1_sw2), .sw3(dipswitch_1_sw3), .sw4(dipswitch_1_sw4),
    .sw5(dipswitch_1_sw5), .sw6(dipswitch_1_sw6), .sw7(dipswitch_1_sw7), .sw8(dipswitch_1_sw8));
  DipSwitch dipswitch_2 (
    .sw1(dipswitch_2_sw1), .sw2(dipswitch_2_sw2), .sw3(dipswitch_2_sw3), .sw4(dipswitch_2_sw4),
    .sw5(dipswitch_2_sw5), .sw6(dipswitch_2_sw6), .sw7(dipswitch_2_sw7), .sw8(dipswitch_2_sw8));
  DipSwitch dipswitch_3 (
    .sw1(dipswitch_3_sw1), .sw2(dipswitch_3_sw2), .sw3(dipswitch_3_sw3), .sw4(dipswitch_3_sw4),
    .sw5(dipswitch_3_sw5), .sw6(dipswitch_3_sw6), .sw7(dipswitch_3_sw7), .sw8(dipswitch_3_sw8));
  DipSwitch dipswitch_4 (
    .sw1(dipswitch_4_sw1), .sw2(dipswitch_4_sw2), .sw3(dipswitch_4_sw3), .sw4(dipswitch_4_sw4),
    .sw5(dipswitch_4_sw5), .sw6(dipswitch_4_sw6), .sw7(dipswitch_4_sw7), .sw8(dipswitch_4_sw8));
  DipSwitch dipswitch_5 (
    .sw1(dipswitch_5_sw1), .sw2(dipswitch_5_sw2), .sw3(dipswitch_5_sw3), .sw4(dipswitch_5_sw4),
    .sw5(dipswitch_5_sw5), .sw6(dipswitch_5_sw6), .sw7(dipswitch_5_sw7), .sw8(dipswitch_5_sw8));
  DipSwitch dipswitch_6 (
    .sw1(dipswitch_6_sw1), .sw2(dipswitch_6_sw2), .sw3(dipswitch_6_sw3), .sw4(dipswitch_6_sw4),
    .sw5(dipswitch_6_sw5), .sw6(dipswitch_6_sw6), .sw7(dipswitch_6_sw7), .sw8(dipswitch_6_sw8));
  DipSwitch dipswitch_7 (
    .sw1(dipswitch_7_sw1), .sw2(dipswitch_7_sw2), .sw3(dipswitch_7_sw3), .sw4(dipswitch_7_sw4),
    .sw5(dipswitch_7_sw5), .sw6(dipswitch_7_sw6), .sw7(dipswitch_7_sw7), .sw8(dipswitch_7_sw8));
  Adder_8_bit adder_8_bit_1 (
    .A1(dipswitch_1_sw1), .A2(dipswitch_1_sw2), .A3(dipswitch_1_sw3), .A4(dipswitch_1_sw4),
    .A5(dipswitch_1_sw5), .A6(dipswitch_1_sw6), .A7(dipswitch_1_sw7), .A8(dipswitch_1_sw8),
    .B1(dipswitch_6_sw1), .B2(dipswitch_6_sw2), .B3(dipswitch_6_sw3), .B4(dipswitch_6_sw4),
    .B5(dipswitch_6_sw5), .B6(dipswitch_6_sw6), .B7(dipswitch_6_sw7), .B8(dipswitch_6_sw8),
    .O1(adder_8_bit_1_o1), .O2(adder_8_bit_1_o2), .O3(adder_8_bit_1_o3), .O4(adder_8_bit_1_o4),
    .O5(adder_8_bit_1_o5), .O6(adder_8_bit_1_o6), .O7(adder_8_bit_1_o7), .O8(adder_8_bit_1_o8),
    .C_OUT(adder_8_bit_1_c_out));
  LED led_1 (.in(adder_8_bit_1_c_out));
  AND_8_bit and_8_bit_1 (
    .A1(dipswitch_2_sw1), .A2(dipswitch_2_sw2), .A3(dipswitch_2_sw3), .A4(dipswitch_2_sw4),
    .A5(dipswitch_2_sw5), .A6(dipswitch_2_sw6), .A7(dipswitch_2_sw7), .A8(dipswitch_2_sw8),
    .B1(dipswitch_3_sw1), .B2(dipswitch_3_sw2), .B3(dipswitch_3_sw3), .B4(dipswitch_3_sw4),
    .B5(dipswitch_3_sw5), .B6(dipswitch_3_sw6), .B7(dipswitch_3_sw7), .B8(dipswitch_3_sw8),
    .O1(and_8_bit_1_o1), .O2(and_8_bit_1_o2), .O3(and_8_bit_1_o3), .O4(and_8_bit_1_o4), .O5(and_8_bit_1_o5),
    .O6(and_8_bit_1_o6), .O7(and_8_bit_1_o7), .O8(and_8_bit_1_o8));
  DipSwitch dipswitch_8 (.sw1(dipswitch_8_sw1), .sw2(dipswitch_8_sw2));  // open: sw3, sw4, sw5, sw6, sw7, sw8
  OR_8_bit or_8_bit_1 (
    .A1(dipswitch_4_sw1), .A2(dipswitch_4_sw2), .A3(dipswitch_4_sw3), .A4(dipswitch_4_sw4),
    .A5(dipswitch_4_sw5), .A6(dipswitch_4_sw6), .A7(dipswitch_4_sw7), .A8(dipswitch_4_sw8),
    .B1(dipswitch_5_sw1), .B2(dipswitch_5_sw2), .B3(dipswitch_5_sw3), .B4(dipswitch_5_sw4),
    .B5(dipswitch_5_sw5), .B6(dipswitch_5_sw6), .B7(dipswitch_5_sw7), .B8(dipswitch_5_sw8),
    .O1(or_8_bit_1_o1), .O2(or_8_bit_1_o2), .O3(or_8_bit_1_o3), .O4(or_8_bit_1_o4), .O5(or_8_bit_1_o5),
    .O6(or_8_bit_1_o6), .O7(or_8_bit_1_o7), .O8(or_8_bit_1_o8));
  Button button_1 (.out(button_1_out));
  DipSwitch dipswitch_9 (
    .sw1(dipswitch_9_sw1), .sw2(dipswitch_9_sw2), .sw3(dipswitch_9_sw3), .sw4(dipswitch_9_sw4),
    .sw5(dipswitch_9_sw5), .sw6(dipswitch_9_sw6), .sw7(dipswitch_9_sw7), .sw8(dipswitch_9_sw8));
  DipSwitch dipswitch_10 (
    .sw1(dipswitch_10_sw1), .sw2(dipswitch_10_sw2), .sw3(dipswitch_10_sw3), .sw4(dipswitch_10_sw4),
    .sw5(dipswitch_10_sw5), .sw6(dipswitch_10_sw6), .sw7(dipswitch_10_sw7), .sw8(dipswitch_10_sw8));
  LED led_2 (.in(mux_8_bit_4_to_1_1_o1));
  MUX_8_bit_4_to_1 mux_8_bit_4_to_1_1 (
    .A1(adder_8_bit_1_o8), .A2(adder_8_bit_1_o7), .A3(adder_8_bit_1_o6), .A4(adder_8_bit_1_o5),
    .A5(adder_8_bit_1_o4), .A6(adder_8_bit_1_o3), .A7(adder_8_bit_1_o2), .A8(adder_8_bit_1_o1),
    .B1(and_8_bit_1_o1), .B2(and_8_bit_1_o2), .B3(and_8_bit_1_o3), .B4(and_8_bit_1_o4), .B5(and_8_bit_1_o5),
    .B6(and_8_bit_1_o6), .B7(and_8_bit_1_o7), .B8(and_8_bit_1_o8), .S0(dipswitch_8_sw1),
    .S1(dipswitch_8_sw2), .C1(or_8_bit_1_o1), .C2(or_8_bit_1_o2), .C3(or_8_bit_1_o3), .C4(or_8_bit_1_o4),
    .C5(or_8_bit_1_o5), .C6(or_8_bit_1_o6), .C7(or_8_bit_1_o7), .C8(or_8_bit_1_o8), .D1(xor_8_bit_1_o1),
    .D2(xor_8_bit_1_o2), .D3(xor_8_bit_1_o3), .D4(xor_8_bit_1_o4), .D5(xor_8_bit_1_o5), .D6(xor_8_bit_1_o6),
    .D7(xor_8_bit_1_o7), .O1(mux_8_bit_4_to_1_1_o1), .O2(mux_8_bit_4_to_1_1_o2), .O3(mux_8_bit_4_to_1_1_o3),
    .O4(mux_8_bit_4_to_1_1_o4), .O5(mux_8_bit_4_to_1_1_o5), .O6(mux_8_bit_4_to_1_1_o6),
    .O7(mux_8_bit_4_to_1_1_o7), .O8(mux_8_bit_4_to_1_1_o8));  // open: D8
  LED led_3 (.in(mux_8_bit_4_to_1_1_o2));
  LED led_4 (.in(mux_8_bit_4_to_1_1_o3));
  LED led_5 (.in(mux_8_bit_4_to_1_1_o4));
  LED led_6 (.in(mux_8_bit_4_to_1_1_o5));
  LED led_7 (.in(mux_8_bit_4_to_1_1_o6));
  LED led_8 (.in(mux_8_bit_4_to_1_1_o7));
  LED led_9 (.in(mux_8_bit_4_to_1_1_o8));
  LED led_10 (.in(register8_1_q1));
  Register8 register8_1 (
    .D1(dipswitch_7_sw1), .D2(dipswitch_7_sw2), .D3(dipswitch_7_sw3), .D4(dipswitch_7_sw4),
    .D5(dipswitch_7_sw5), .D6(dipswitch_7_sw6), .D7(dipswitch_7_sw7), .D8(dipswitch_7_sw8),
    .CLOCK(button_1_out), .WE(button_1_out), .Q1(register8_1_q1), .Q2(register8_1_q2), .Q3(register8_1_q3),
    .Q4(register8_1_q4), .Q5(register8_1_q5), .Q6(register8_1_q6), .Q7(register8_1_q7), .Q8(register8_1_q8));
  LED led_11 (.in(register8_1_q2));
  LED led_12 (.in(register8_1_q3));
  LED led_13 (.in(register8_1_q4));
  LED led_14 (.in(register8_1_q5));
  LED led_15 (.in(register8_1_q6));
  LED led_16 (.in(register8_1_q7));
  LED led_17 (.in(register8_1_q8));
  XOR_8_bit xor_8_bit_1 (
    .A1(dipswitch_9_sw1), .A2(dipswitch_9_sw2), .A3(dipswitch_9_sw3), .A4(dipswitch_9_sw4),
    .A5(dipswitch_9_sw5), .A6(dipswitch_9_sw6), .A7(dipswitch_9_sw7), .A8(dipswitch_9_sw8),
    .B1(dipswitch_10_sw1), .B2(dipswitch_10_sw2), .B3(dipswitch_10_sw3), .B4(dipswitch_10_sw4),
    .B5(dipswitch_10_sw5), .B6(dipswitch_10_sw6), .B7(dipswitch_10_sw7), .B8(dipswitch_10_sw8),
    .O1(xor_8_bit_1_o1), .O2(xor_8_bit_1_o2), .O3(xor_8_bit_1_o3), .O4(xor_8_bit_1_o4), .O5(xor_8_bit_1_o5),
    .O6(xor_8_bit_1_o6), .O7(xor_8_bit_1_o7), .O8(xor_8_bit_1_o8));
endmodule

module FullAdder (
  input  A,
  input  B,
  input  Carry_In,
  output Carry_Out,
  output Sum
);

  wire and_1_out, and_2_out, xor_1_out;

  and and_1 (and_1_out, A, B);
  xor xor_1 (xor_1_out, A, B);
  xor xor_2 (Sum, xor_1_out, Carry_In);
  and and_2 (and_2_out, xor_1_out, Carry_In);
  or or_1 (Carry_Out, and_1_out, and_2_out);
endmodule

module Adder_8_bit (
  input  A1,
  input  A2,
  input  A3,
  input  A4,
  input  A5,
  input  A6,
  input  A7,
  input  A8,
  input  B1,
  input  B2,
  input  B3,
  input  B4,
  input  B5,
  input  B6,
  input  B7,
  input  B8,
  output O1,
  output O2,
  output O3,
  output O4,
  output O5,
  output O6,
  output O7,
  output O8,
  output C_OUT
);

  wire fulladder_2_carry_out, fulladder_3_carry_out, fulladder_4_carry_out, fulladder_5_carry_out,
       fulladder_6_carry_out, fulladder_7_carry_out, fulladder_8_carry_out;

  FullAdder fulladder_1 (.A(A1), .B(B1), .Carry_In(fulladder_2_carry_out), .Carry_Out(C_OUT), .Sum(O8));
  FullAdder fulladder_2 (.A(A2), .B(B2), .Carry_In(fulladder_3_carry_out), .Carry_Out(fulladder_2_carry_out), .Sum(O7));
  FullAdder fulladder_3 (.A(A3), .B(B3), .Carry_In(fulladder_4_carry_out), .Carry_Out(fulladder_3_carry_out), .Sum(O6));
  FullAdder fulladder_4 (.A(A4), .B(B4), .Carry_In(fulladder_5_carry_out), .Carry_Out(fulladder_4_carry_out), .Sum(O5));
  FullAdder fulladder_5 (.A(A5), .B(B5), .Carry_In(fulladder_6_carry_out), .Carry_Out(fulladder_5_carry_out), .Sum(O4));
  FullAdder fulladder_6 (.A(A6), .B(B6), .Carry_In(fulladder_7_carry_out), .Carry_Out(fulladder_6_carry_out), .Sum(O3));
  FullAdder fulladder_7 (.A(A7), .B(B7), .Carry_In(fulladder_8_carry_out), .Carry_Out(fulladder_7_carry_out), .Sum(O2));
  FullAdder fulladder_8 (.A(A8), .B(B8), .Carry_In(1'b0), .Carry_Out(fulladder_8_carry_out), .Sum(O1));
endmodule

module AND_8_bit (
  input  A1,
  input  A2,
  input  A3,
  input  A4,
  input  A5,
  input  A6,
  input  A7,
  input  A8,
  input  B1,
  input  B2,
  input  B3,
  input  B4,
  input  B5,
  input  B6,
  input  B7,
  input  B8,
  output O1,
  output O2,
  output O3,
  output O4,
  output O5,
  output O6,
  output O7,
  output O8
);

  and and_1 (O1, A1, B1);
  and and_2 (O2, A2, B2);
  and and_3 (O3, A3, B3);
  and and_4 (O4, A4, B4);
  and and_5 (O5, A5, B5);
  and and_6 (O6, A6, B6);
  and and_7 (O7, A7, B7);
  and and_8 (O8, A8, B8);
endmodule

module OR_8_bit (
  input  A1,
  input  A2,
  input  A3,
  input  A4,
  input  A5,
  input  A6,
  input  A7,
  input  A8,
  input  B1,
  input  B2,
  input  B3,
  input  B4,
  input  B5,
  input  B6,
  input  B7,
  input  B8,
  output O1,
  output O2,
  output O3,
  output O4,
  output O5,
  output O6,
  output O7,
  output O8
);

  or or_1 (O1, A1, B1);
  or or_2 (O2, A2, B2);
  or or_3 (O3, A3, B3);
  or or_4 (O4, A4, B4);
  or or_5 (O5, A5, B5);
  or or_6 (O6, A6, B6);
  or or_7 (O7, A7, B7);
  or or_8 (O8, A8, B8);
endmodule

module XOR_8_bit (
  input  A1,
  input  A2,
  input  A3,
  input  A4,
  input  A5,
  input  A6,
  input  A7,
  input  A8,
  input  B1,
  input  B2,
  input  B3,
  input  B4,
  input  B5,
  input  B6,
  input  B7,
  input  B8,
  output O1,
  output O2,
  output O3,
  output O4,
  output O5,
  output O6,
  output O7,
  output O8
);

  xor xor_1 (O1, A1, B1);
  xor xor_2 (O2, A2, B2);
  xor xor_3 (O3, A3, B3);
  xor xor_4 (O4, A4, B4);
  xor xor_5 (O5, A5, B5);
  xor xor_6 (O6, A6, B6);
  xor xor_7 (O7, A7, B7);
  xor xor_8 (O8, A8, B8);
endmodule

module My_Multiplexer (
  input  A,
  input  B,
  input  S,
  output O
);

  wire and_1_out, and_2_out, not_1_out;

  not not_1 (not_1_out, S);
  and and_1 (and_1_out, A, not_1_out);
  and and_2 (and_2_out, B, S);
  or or_1 (O, and_1_out, and_2_out);
endmodule

module MUX_4to1 (
  input  I0,
  input  I1,
  input  I2,
  input  I3,
  input  S1,
  input  S0,
  output O
);

  wire my_multiplexer_1_o, my_multiplexer_2_o;

  My_Multiplexer my_multiplexer_1 (.A(I0), .B(I1), .S(S1), .O(my_multiplexer_1_o));
  My_Multiplexer my_multiplexer_2 (.A(I2), .B(I3), .S(S1), .O(my_multiplexer_2_o));
  My_Multiplexer my_multiplexer_3 (.A(my_multiplexer_1_o), .B(my_multiplexer_2_o), .S(S0), .O(O));
endmodule

module MUX_8_bit_4_to_1 (
  input  A1,
  input  A2,
  input  A3,
  input  A4,
  input  A5,
  input  A6,
  input  A7,
  input  A8,
  input  B1,
  input  B2,
  input  B3,
  input  B4,
  input  B5,
  input  B6,
  input  B7,
  input  B8,
  input  S0,
  input  S1,
  input  C1,
  input  C2,
  input  C3,
  input  C4,
  input  C5,
  input  C6,
  input  C7,
  input  C8,
  input  D1,
  input  D2,
  input  D3,
  input  D4,
  input  D5,
  input  D6,
  input  D7,
  input  D8,
  output O1,
  output O2,
  output O3,
  output O4,
  output O5,
  output O6,
  output O7,
  output O8
);

  MUX_4to1 mux_4to1_1 (.I0(A1), .I1(B1), .I2(C1), .I3(D1), .S1(S1), .S0(S0), .O(O1));
  MUX_4to1 mux_4to1_2 (.I0(A2), .I1(B2), .I2(C2), .I3(D2), .S1(S1), .S0(S0), .O(O2));
  MUX_4to1 mux_4to1_3 (.I0(A3), .I1(B3), .I2(C3), .I3(D3), .S1(S1), .S0(S0), .O(O3));
  MUX_4to1 mux_4to1_4 (.I0(A4), .I1(B4), .I2(C4), .I3(D4), .S1(S1), .S0(S0), .O(O4));
  MUX_4to1 mux_4to1_5 (.I0(A5), .I1(B5), .I2(C5), .I3(D5), .S1(S1), .S0(S0), .O(O5));
  MUX_4to1 mux_4to1_6 (.I0(A6), .I1(B6), .I2(C6), .I3(D6), .S1(S1), .S0(S0), .O(O6));
  MUX_4to1 mux_4to1_7 (.I0(A7), .I1(B7), .I2(C7), .I3(D7), .S1(S1), .S0(S0), .O(O7));
  MUX_4to1 mux_4to1_8 (.I0(A8), .I1(B8), .I2(C8), .I3(D8), .S1(S1), .S0(S0), .O(O8));
endmodule

module SR_Latch (
  input  CLK,
  input  D,
  output Q
);

  wire and_1_out, and_2_out, and_3_out, and_4_out, nor_1_out, nor_2_out, nor_3_out, not_1_out, not_2_out,
       not_3_out;

  and and_1 (and_1_out, CLK, D);
  not not_1 (not_1_out, CLK);
  and and_2 (and_2_out, not_1_out, nor_3_out);
  nor nor_1 (nor_1_out, and_1_out, nor_3_out);
  not not_2 (not_2_out, D);
  and and_3 (and_3_out, not_2_out, CLK);
  nor nor_2 (nor_2_out, and_2_out, Q);
  not not_3 (not_3_out, nor_3_out);
  nor nor_3 (nor_3_out, nor_1_out, and_3_out);
  and and_4 (and_4_out, not_3_out, not_1_out);
  nor nor_4 (Q, nor_2_out, and_4_out);
endmodule

module Register8 (
  input  D1,
  input  D2,
  input  D3,
  input  D4,
  input  D5,
  input  D6,
  input  D7,
  input  D8,
  input  CLOCK,
  input  WE,
  output Q1,
  output Q2,
  output Q3,
  output Q4,
  output Q5,
  output Q6,
  output Q7,
  output Q8
);

  wire mux_8_bit_4_to_1_1_o1, mux_8_bit_4_to_1_1_o2, mux_8_bit_4_to_1_1_o3, mux_8_bit_4_to_1_1_o4,
       mux_8_bit_4_to_1_1_o5, mux_8_bit_4_to_1_1_o6, mux_8_bit_4_to_1_1_o7, mux_8_bit_4_to_1_1_o8;

  SR_Latch sr_latch_1 (.CLK(CLOCK), .D(mux_8_bit_4_to_1_1_o1), .Q(Q1));
  SR_Latch sr_latch_2 (.CLK(CLOCK), .D(mux_8_bit_4_to_1_1_o2), .Q(Q2));
  SR_Latch sr_latch_3 (.CLK(CLOCK), .D(mux_8_bit_4_to_1_1_o3), .Q(Q3));
  SR_Latch sr_latch_4 (.CLK(CLOCK), .D(mux_8_bit_4_to_1_1_o4), .Q(Q4));
  SR_Latch sr_latch_5 (.CLK(CLOCK), .D(mux_8_bit_4_to_1_1_o5), .Q(Q5));
  SR_Latch sr_latch_6 (.CLK(CLOCK), .D(mux_8_bit_4_to_1_1_o6), .Q(Q6));
  SR_Latch sr_latch_7 (.CLK(CLOCK), .D(mux_8_bit_4_to_1_1_o7), .Q(Q7));
  SR_Latch sr_latch_8 (.CLK(CLOCK), .D(mux_8_bit_4_to_1_1_o8), .Q(Q8));
  MUX_8_bit_4_to_1 mux_8_bit_4_to_1_1 (
    .A1(Q1), .A2(Q2), .A3(Q3), .A4(Q4), .A5(Q5), .A6(Q6), .A7(Q7), .A8(Q8), .B1(D1), .B2(D2), .B3(D3),
    .B4(D4), .B5(D5), .B6(D6), .B7(D7), .B8(D8), .S0(WE), .O1(mux_8_bit_4_to_1_1_o1),
    .O2(mux_8_bit_4_to_1_1_o2), .O3(mux_8_bit_4_to_1_1_o3), .O4(mux_8_bit_4_to_1_1_o4),
    .O5(mux_8_bit_4_to_1_1_o5), .O6(mux_8_bit_4_to_1_1_o6), .O7(mux_8_bit_4_to_1_1_o7),
    .O8(mux_8_bit_4_to_1_1_o8));  // open: S1, C1, C2, C3, C4, C5, C6, C7, C8, D1, D2, D3, D4, D5, D6, D7, D8
endmodule

module Program_Counter (
);

  wire adder_8_bit_1_c_out, adder_8_bit_1_o1, adder_8_bit_1_o2, adder_8_bit_1_o3, adder_8_bit_1_o4,
       adder_8_bit_1_o5, adder_8_bit_1_o6, adder_8_bit_1_o7, adder_8_bit_1_o8, clock_1_out, register8_1_q1,
       register8_1_q2, register8_1_q3, register8_1_q4, register8_1_q5, register8_1_q6, register8_1_q7,
       register8_1_q8;

  Clock clock_1 (.out(clock_1_out));
  Register8 register8_1 (
    .D1(adder_8_bit_1_o8), .D2(adder_8_bit_1_o7), .D3(adder_8_bit_1_o6), .D4(adder_8_bit_1_o5),
    .D5(adder_8_bit_1_o4), .D6(adder_8_bit_1_o3), .D7(adder_8_bit_1_o2), .D8(adder_8_bit_1_o1),
    .CLOCK(clock_1_out), .WE(1'b1), .Q1(register8_1_q1), .Q2(register8_1_q2), .Q3(register8_1_q3),
    .Q4(register8_1_q4), .Q5(register8_1_q5), .Q6(register8_1_q6), .Q7(register8_1_q7), .Q8(register8_1_q8));
  LED led_1 (.in(adder_8_bit_1_o1));
  Adder_8_bit adder_8_bit_1 (
    .A1(register8_1_q1), .A2(register8_1_q2), .A3(register8_1_q3), .A4(register8_1_q4), .A5(register8_1_q5),
    .A6(register8_1_q6), .A7(register8_1_q7), .A8(register8_1_q8), .B1(1'b0), .B2(1'b0), .B3(1'b0),
    .B4(1'b0), .B5(1'b0), .B6(1'b0), .B7(1'b0), .B8(1'b1), .O1(adder_8_bit_1_o1), .O2(adder_8_bit_1_o2),
    .O3(adder_8_bit_1_o3), .O4(adder_8_bit_1_o4), .O5(adder_8_bit_1_o5), .O6(adder_8_bit_1_o6),
    .O7(adder_8_bit_1_o7), .O8(adder_8_bit_1_o8), .C_OUT(adder_8_bit_1_c_out));
  LED led_2 (.in(adder_8_bit_1_o2));
  LED led_3 (.in(adder_8_bit_1_o3));
  LED led_4 (.in(adder_8_bit_1_o4));
  LED led_5 (.in(adder_8_bit_1_o5));
  LED led_6 (.in(adder_8_bit_1_o6));
  LED led_7 (.in(adder_8_bit_1_o7));
  LED led_8 (.in(adder_8_bit_1_o8));
  LED led_9 (.in(adder_8_bit_1_c_out));
endmodule

module RAM4x8 (
  input  A2
);

  wire decoder_2to4_1_o1, decoder_2to4_1_o2, decoder_2to4_1_o3, decoder_2to4_1_o4, dipswitch_1_sw1,
       dipswitch_1_sw2;

  DipSwitch dipswitch_1 (.sw1(dipswitch_1_sw1), .sw2(dipswitch_1_sw2));  // open: sw3, sw4, sw5, sw6, sw7, sw8
  Decoder_2to4 decoder_2to4_1 (
    .A1(dipswitch_1_sw1), .A2(dipswitch_1_sw2), .O1(decoder_2to4_1_o1), .O2(decoder_2to4_1_o2),
    .O3(decoder_2to4_1_o3), .O4(decoder_2to4_1_o4));
  Register8 register8_1 (.WE(decoder_2to4_1_o1));  // open: D1, D2, D3, D4, D5, D6, D7, D8, CLOCK, Q1, Q2, Q3, Q4, Q5, Q6, Q7, Q8
  Register8 register8_2 (.WE(decoder_2to4_1_o2));  // open: D1, D2, D3, D4, D5, D6, D7, D8, CLOCK, Q1, Q2, Q3, Q4, Q5, Q6, Q7, Q8
  Register8 register8_3 (.WE(decoder_2to4_1_o3));  // open: D1, D2, D3, D4, D5, D6, D7, D8, CLOCK, Q1, Q2, Q3, Q4, Q5, Q6, Q7, Q8
  Register8 register8_4 (.WE(decoder_2to4_1_o4));  // open: D1, D2, D3, D4, D5, D6, D7, D8, CLOCK, Q1, Q2, Q3, Q4, Q5, Q6, Q7, Q8
endmodule

module Decoder_2to4 (
  input  A1,
  input  A2,
  output O1,
  output O2,
  output O3,
  output O4
);

  wire not_1_out, not_2_out;

  not not_1 (not_1_out, A1);
  not not_2 (not_2_out, A2);
  and and_1 (O2, A1, not_2_out);
  and and_2 (O4, A2, A1);
  and and_3 (O3, not_1_out, A2);
  and and_4 (O1, not_1_out, not_2_out);
endmodule
